# Fritzing sketch tinyLCD_I2C (saved by Fritzing 0.7.11b)
breadboards: 1

parts:
  ATtiny84 = IC, DIP package, 14 pins [chip_label=ATtiny84A]
  I2C = male pin header, 4 pins [form="♂ (male)"]
  LCD = male pin header, 16 pins [form="♂ (male)"]
  ICSP = shrouded pin header, 6 pins [form="♂ (shrouded male)"]
  R2 = Resistor [tolerance=±5% resistance=4.7k package=THT]
  C1 = Ceramic Capacitor [capacitance=4.7µF package="100 mil [THT, multilayer]"]
  R3 = Resistor [tolerance=±5% resistance=150 package=THT]
  D10 = male pin header, 4 pins [form="♂ (male)"]

nets:
  N1: ATtiny84.pin1, I2C.pin1, LCD.pin2, ICSP.pin6, D10.pin2
  N2: ATtiny84.pin2, LCD.pin4
  N3: ATtiny84.pin3, LCD.pin6
  N4: ATtiny84.pin4, ICSP.pin3, D10.pin1
  N5: ATtiny84.pin5, R2.Pin_0
  N6: ATtiny84.pin6, R3.Pin_0
  N7: ATtiny84.pin7, I2C.pin2, ICSP.pin5
  N8: ATtiny84.pin8, LCD.pin14, ICSP.pin1
  N9: ATtiny84.pin9, I2C.pin3, ICSP.pin2
  N10: ATtiny84.pin10, LCD.pin13
  N11: ATtiny84.pin11, LCD.pin12
  N12: ATtiny84.pin12, LCD.pin11
  N13: ATtiny84.pin13, D10.pin3
  N14: ATtiny84.pin14, I2C.pin4, LCD.pin1, LCD.pin5, LCD.pin16, ICSP.pin4, C1.1, D10.pin4
  N15: LCD.pin3, R2.Pin_1, C1.0
  N16: LCD.pin15, R3.Pin_1

notes:
  VCC SDA SCL GND
  GND VCC V0 RS R/W EN D0 D1 D2 D3 D4 D5 D6 D7 L+ L-
  (1)                                          (16)
  GND|SCL|SDA|VCC
  tinyLCD-I2C v1.0
  http://boxtec.ch
  (1)                                                                                           (16)
  GND | MOSI | VCC
  RST | SCK | MISO
  RST|VCC|D10|GND
